// Logisim project cricuit.circ as structural Verilog: 13 circuits, main circuit main
module main (
);

  wire clock_1_out, pd_mine_1_f7, pd_mine_1_zero, uc_1_out_6, uc_1_out_9, uc_1_out_10, uc_1_out_11;
  wire [1:0] uc_1_out_7, uc_1_out_8, uc_1_out_12;
  wire [2:0] pd_mine_1_f3, uc_1_out_5;
  wire [6:0] pd_mine_1_op;
  wire [15:0] pd_mine_1_out_11;
  wire [31:0] memory_1_out_6, memory_1_out_7, pd_mine_1_out_15, pd_mine_1_out_17;

  Clock clock_1 (.out(clock_1_out));
  UC uc_1 (
    .in_1(pd_mine_1_op), .in_2(pd_mine_1_f7), .in_3(pd_mine_1_f3), .out_5(uc_1_out_5), .out_6(uc_1_out_6),
    .out_7(uc_1_out_7), .out_8(uc_1_out_8), .out_9(uc_1_out_9), .out_10(uc_1_out_10), .out_11(uc_1_out_11),
    .out_12(uc_1_out_12), .in_4(pd_mine_1_zero));
  pd_mine pd_mine_1 (
    .in_9(uc_1_out_12), .in_10(uc_1_out_8), .out_11(pd_mine_1_out_11), .f7(pd_mine_1_f7), .f3(pd_mine_1_f3),
    .op(pd_mine_1_op), .out_15(pd_mine_1_out_15), .zero(pd_mine_1_zero), .out_17(pd_mine_1_out_17),
    .branch(uc_1_out_6), .jump(uc_1_out_7), .clk(clock_1_out), .en(uc_1_out_11), .aluSrc(uc_1_out_10),
    .aluControl(uc_1_out_5), .immSrc(memory_1_out_7), .resSrc(memory_1_out_6));
  Memory memory_1 (
    .in_1(clock_1_out), .in_2(uc_1_out_9), .in_3(pd_mine_1_out_17[15:0]), .in_4(pd_mine_1_out_15),
    .in_5(pd_mine_1_out_11), .out_6(memory_1_out_6), .out_7(memory_1_out_7));
endmodule

module pc (
  input  in_1,
  input  [15:0] in_2,
  output [15:0] out_3
);
endmodule

module SE (
  input  [31:0] in_1,
  input  [1:0] in_2,
  output [31:0] out_3
);
endmodule

module BR (
  input  in_1,
  input  [4:0] in_2,
  input  [4:0] in_3,
  input  [4:0] in_4,
  input  [31:0] in_5,
  input  in_6,
  output [31:0] out_7,
  output [31:0] out_8
);
endmodule

module ALU (
  input  [31:0] in_1,
  input  [31:0] in_2,
  input  [2:0] in_3,
  output [31:0] out_4,
  output out_5
);
endmodule

module data_path (
  input  [31:0] in_1,
  input  [31:0] in_2,
  input  branch,
  input  jump,
  input  clk,
  input  [1:0] resultSrc,
  input  [1:0] inmSrc,
  input  regWrite,
  input  ALUSrc,
  input  [2:0] ALUControl,
  output [31:0] out_11,
  output zero,
  output [6:0] out_13,
  output [2:0] f3,
  output f7,
  output [31:0] out_16,
  output [15:0] out_17
);

  wire [15:0] adder_1_out, adder_2_out, multiplexer_1_out, multiplexer_2_out;
  wire [31:0] bit_extender_1_out, br_1_out_7, multiplexer_3_out, multiplexer_4_out, se_1_out_3;

  Multiplexer #(.width(16)) multiplexer_1 (
    .in0(16'h4), .in1(se_1_out_3[15:0]), .out(multiplexer_1_out), .sel(branch));  // open: en
  Adder #(.width(16)) adder_1 (.a(multiplexer_1_out), .b(out_17), .out(adder_1_out));  // open: cin, cout
  Adder #(.width(16)) adder_2 (.a(se_1_out_3[15:0]), .b(out_17), .out(adder_2_out));  // open: cin, cout
  Multiplexer #(.width(16)) multiplexer_2 (
    .in0(adder_1_out), .in1(adder_2_out), .out(multiplexer_2_out), .sel(jump));  // open: en
  pc pc_1 (.in_1(clk), .in_2(multiplexer_2_out), .out_3(out_17));
  assign bit_extender_1_out = {{16{1'b0}}, adder_1_out};  // Bit_Extender bit_extender_1
  Multiplexer #(.select(2), .width(32)) multiplexer_3 (
    .in0(out_11), .in1(in_1), .in2(se_1_out_3), .in3(bit_extender_1_out), .out(multiplexer_3_out),
    .sel(resultSrc));  // open: en
  BR br_1 (
    .in_1(clk), .in_2(in_2[19:15]), .in_3(in_2[24:20]), .in_4(in_2[11:7]), .in_5(multiplexer_3_out),
    .in_6(regWrite), .out_7(br_1_out_7), .out_8(out_16));
  SE se_1 (.in_1(in_2), .in_2(inmSrc), .out_3(se_1_out_3));
  Multiplexer #(.width(32)) multiplexer_4 (
    .in0(out_16), .in1(se_1_out_3), .out(multiplexer_4_out), .sel(ALUSrc));  // open: en
  ALU alu_1 (.in_1(br_1_out_7), .in_2(multiplexer_4_out), .in_3(ALUControl), .out_4(out_11), .out_5(zero));

  assign f3 = in_2[14:12];
  assign f7 = in_2[30];
  assign out_13 = in_2[6:0];

  // Notes on the sheet:
  //   s_pcPlus
  //   add4
  //   s_pcnext
  //   addJump
  //   s_pcJump
  //   readData
  //   inst
  //   s_src2
  //   pc
  //   ALURes
  //   opcode
  //   writeData
endmodule

module pd_mine (
  input  branch,
  input  [1:0] jump,
  input  clk,
  input  en,
  input  aluSrc,
  input  [2:0] aluControl,
  input  [31:0] immSrc,
  input  [31:0] resSrc,
  input  [1:0] in_9,
  input  [1:0] in_10,
  output [15:0] out_11,
  output f7,
  output [2:0] f3,
  output [6:0] op,
  output [31:0] out_15,
  output zero,
  output [31:0] out_17
);

  wire [31:0] adder_1_out, adder_2_out, bit_extender_1_out, bit_extender_2_out, br_1_out_7,
       multiplexer_1_out, multiplexer_2_out, multiplexer_3_out, multiplexer_4_out, se_1_out_3;

  Multiplexer #(.width(32)) multiplexer_1 (
    .in0(32'h4), .in1(se_1_out_3), .out(multiplexer_1_out), .sel(branch));  // open: en
  assign bit_extender_1_out = {{16{1'b0}}, out_11};  // Bit_Extender bit_extender_1
  assign bit_extender_2_out = {{16{1'b0}}, out_11};  // Bit_Extender bit_extender_2
  Adder #(.width(32)) adder_1 (.a(multiplexer_1_out), .b(bit_extender_1_out), .out(adder_1_out));  // open: cin, cout
  Adder #(.width(32)) adder_2 (.a(bit_extender_2_out), .b(se_1_out_3), .out(adder_2_out));  // open: cin, cout
  Multiplexer #(.select(2), .width(32)) multiplexer_2 (
    .in0({32{1'b0}}), .in1(adder_1_out), .in2(adder_2_out), .out(multiplexer_2_out), .sel(jump));  // open: in3, en
  pc pc_1 (.in_1(clk), .in_2(multiplexer_2_out[15:0]), .out_3(out_11));
  SE se_1 (.in_1(immSrc), .in_2(in_9), .out_3(se_1_out_3));
  Multiplexer #(.select(2), .width(32)) multiplexer_3 (
    .in0(out_17), .in1(se_1_out_3), .in2(resSrc), .in3(adder_1_out), .out(multiplexer_3_out), .sel(in_10));  // open: en
  BR br_1 (
    .in_1(clk), .in_2(immSrc[19:15]), .in_3(immSrc[24:20]), .in_4(immSrc[11:7]), .in_5(multiplexer_3_out),
    .in_6(en), .out_7(br_1_out_7), .out_8(out_15));
  Multiplexer #(.width(32)) multiplexer_4 (
    .in0(out_15), .in1(se_1_out_3), .out(multiplexer_4_out), .sel(aluSrc));  // open: en
  ALU alu_1 (.in_1(br_1_out_7), .in_2(multiplexer_4_out), .in_3(aluControl), .out_4(out_17), .out_5(zero));

  assign f3 = immSrc[14:12];
  assign f7 = immSrc[30];
  assign op = immSrc[6:0];

  // Notes on the sheet:
  //   m4
  //   s_inmExt
  //   add1
  //   s_pc_offset
  //   s_pc
  //   s_inmExt
  //   pc_jump
  //   m1
  //   pc_next
  //   instr
  //   pc
  //   m3
  //   readData
  //   s_inmExt
  //   s_alu_res
  //   s_srcA
  //   s_src2
  //   writeData
  //   s_srcB
  //   m2
  //   aluRes
endmodule

module DM (
  input  in_1,
  input  in_2,
  input  [15:0] in_3,
  input  [31:0] in_4,
  output [31:0] out_5
);
endmodule

module IM (
  input  [15:0] in_1,
  output [31:0] out_2
);
endmodule

module Memory (
  input  in_1,
  input  in_2,
  input  [15:0] in_3,
  input  [31:0] in_4,
  input  [15:0] in_5,
  output [31:0] out_6,
  output [31:0] out_7
);

  DM dm_1 (.in_1(in_1), .in_2(in_2), .in_3(in_3), .in_4(in_4), .out_5(out_6));
  IM im_1 (.in_1(in_5), .out_2(out_7));
endmodule

module mainDeco (
  input  [6:0] in_1,
  output branch,
  output [1:0] jump,
  output [1:0] resSrc,
  output memWrite,
  output aluSrc,
  output [1:0] immSrc,
  output regWrite,
  output [1:0] aluOp
);
endmodule

module ALUDeco (
  input  in_1,
  input  in_2,
  input  [2:0] in_3,
  input  [1:0] in_4,
  output [2:0] out_5
);
endmodule

module UC (
  input  [6:0] in_1,
  input  in_2,
  input  [2:0] in_3,
  input  in_4,
  output [2:0] out_5,
  output out_6,
  output [1:0] out_7,
  output [1:0] out_8,
  output out_9,
  output out_10,
  output out_11,
  output [1:0] out_12
);

  wire [1:0] maindeco_1_aluop;

  ALUDeco aludeco_1 (.in_1(in_1[5]), .in_2(in_2), .in_3(in_3), .in_4(maindeco_1_aluop), .out_5(out_5));
  mainDeco maindeco_1 (
    .in_1(in_1), .branch(out_6), .jump(out_7), .resSrc(out_8), .memWrite(out_9), .aluSrc(out_10),
    .immSrc(out_12), .regWrite(out_11), .aluOp(maindeco_1_aluop));
endmodule
